# Fritzing sketch ResQ PCB  (saved by Fritzing 0.9.3b)
breadboards: 1

parts:
  WeMos_D1_Mini1 = WeMos D1 Mini
  VCC = Battery
  OLED = female pin header, 6 pins [form="♀ (female)"]  # not connected
  GPS = female pin header, 6 pins [form="♀ (female)"]  # not connected
  SD_Card = female pin header, 6 pins [form="♀ (female)"]  # not connected

nets:
  N1: WeMos_D1_Mini1.5V, VCC.-
  GND: WeMos_D1_Mini1.G, VCC.+
