# Fritzing sketch ResQ PCB V1.1 Routing  (saved by Fritzing 0.9.3b)
breadboards: 1

parts:
  SD_Card = female pin header, 6 pins [form="♀ (female)"]
  OLED = female pin header, 4 pins [form="♀ (female)"]
  Vin = female pin header, 2 pins [form="♀ (female)"]
  WeMos_D1_Mini1 = WeMos D1 Mini
  SP1 = female pin header, 3 pins [form="♀ (female)"]  # not connected
  SP2 = female pin header, 3 pins [form="♀ (female)"]  # not connected
  GPS = female pin header, 4 pins [form="♀ (female)"]

nets:
  N1: SD_Card.pin1, WeMos_D1_Mini1.3V3, GPS.pin4
  CS: SD_Card.pin2, WeMos_D1_Mini1.D8
  MOSI: SD_Card.pin3, WeMos_D1_Mini1.D7
  CLK: SD_Card.pin4, WeMos_D1_Mini1.D5
  MISO: SD_Card.pin5, WeMos_D1_Mini1.D6
  GND: SD_Card.pin6, OLED.pin2, Vin.pin2, WeMos_D1_Mini1.G
  N2: OLED.pin3, WeMos_D1_Mini1.D1
  N3: OLED.pin4, WeMos_D1_Mini1.D2
  N4: Vin.pin1, WeMos_D1_Mini1.5V
  N5: WeMos_D1_Mini1.D3, GPS.pin3
  N6: WeMos_D1_Mini1.D4, GPS.pin2

notes:
  ResQ Search and Rescue Tool, 1.1
